// Logisim project Guia06_3.circ as structural Verilog: 1 circuit, main circuit main
module main (
  input  w,
  input  X,
  input  Y,
  input  Z,
  input  w_2,
  input  X_2,
  input  Y_2,
  input  Z_2,
  input  w_3,
  input  X_3,
  input  Y_3,
  input  Z_3,
  input  w_4,
  input  X_4,
  input  Y_4,
  input  Z_4,
  input  w_5,
  input  X_5,
  input  Y_5,
  input  Z_5,
  output out_21,
  output out_22,
  output out_23,
  output out_24,
  output out_25,
  output out_26,
  output out_27,
  output out_28,
  output out_29,
  output out_30
);

  wire and_1_out, and_2_out, and_3_out, and_4_out, and_5_out, and_6_out, and_7_out, and_8_out, and_9_out,
       and_10_out, and_11_out, and_12_out, and_13_out, and_14_out, and_15_out, and_16_out, and_17_out,
       and_18_out, and_19_out, and_20_out, and_21_out, and_22_out, and_23_out, and_24_out, and_25_out,
       and_26_out, and_27_out, and_28_out, and_29_out, and_30_out, and_31_out, and_32_out, and_33_out,
       and_34_out, and_35_out, and_36_out, and_37_out, and_38_out, and_39_out, and_40_out, and_41_out,
       and_42_out, and_43_out, and_44_out, and_45_out, and_46_out, and_47_out, and_48_out, and_49_out,
       and_50_out, and_51_out, and_52_out, and_53_out, and_54_out, and_55_out, and_56_out, not_1_out,
       not_2_out, not_3_out, not_4_out, not_5_out, not_6_out, not_7_out, not_8_out, not_9_out, not_10_out,
       not_11_out, not_12_out, not_13_out, not_14_out, not_15_out, not_16_out, not_17_out, not_18_out,
       not_19_out, not_20_out;

  not not_1 (not_1_out, w_2);
  not not_2 (not_2_out, X_2);
  not not_3 (not_3_out, Z_2);
  not not_4 (not_4_out, Y_2);
  // AND_Gate and_1 has open pins: out=and_1_out
  // AND_Gate and_2 has open pins: out=and_2_out
  or or_1 (out_21, and_1_out, and_2_out, and_3_out);
  // AND_Gate and_3 has open pins: out=and_3_out
  // AND_Gate and_4 has open pins: out=and_4_out
  // AND_Gate and_5 has open pins: out=and_5_out
  // AND_Gate and_6 has open pins: out=and_6_out
  // AND_Gate and_7 has open pins: out=and_7_out
  // AND_Gate and_8 has open pins: out=and_8_out
  // AND_Gate and_9 has open pins: out=and_9_out
  or or_2 (out_26, and_4_out, and_5_out, and_6_out, and_7_out, and_8_out, and_9_out);
  not not_5 (not_5_out, w_3);
  not not_6 (not_6_out, Y_3);
  not not_7 (not_7_out, Z_3);
  not not_8 (not_8_out, X_3);
  // AND_Gate and_10 has open pins: out=and_10_out
  // AND_Gate and_11 has open pins: out=and_11_out
  // AND_Gate and_12 has open pins: out=and_12_out
  // AND_Gate and_13 has open pins: out=and_13_out
  // AND_Gate and_14 has open pins: out=and_14_out
  // AND_Gate and_15 has open pins: out=and_15_out
  // AND_Gate and_16 has open pins: out=and_16_out
  // AND_Gate and_17 has open pins: out=and_17_out
  // AND_Gate and_18 has open pins: out=and_18_out
  // AND_Gate and_19 has open pins: out=and_19_out
  // AND_Gate and_20 has open pins: out=and_20_out
  or or_3 (out_22, and_10_out, and_11_out, and_12_out, and_13_out);
  or or_4 (out_27, and_14_out, and_15_out, and_16_out, and_17_out, and_18_out, and_19_out, and_20_out);
  not not_9 (not_9_out, w_5);
  not not_10 (not_10_out, Y_5);
  not not_11 (not_11_out, X_5);
  not not_12 (not_12_out, Z_5);
  // AND_Gate and_21 has open pins: out=and_21_out
  // AND_Gate and_22 has open pins: out=and_22_out
  // AND_Gate and_23 has open pins: out=and_23_out
  // AND_Gate and_24 has open pins: out=and_24_out
  // AND_Gate and_25 has open pins: out=and_25_out
  // AND_Gate and_26 has open pins: out=and_26_out
  // AND_Gate and_27 has open pins: out=and_27_out
  // AND_Gate and_28 has open pins: out=and_28_out
  // AND_Gate and_29 has open pins: out=and_29_out
  // AND_Gate and_30 has open pins: out=and_30_out
  // AND_Gate and_31 has open pins: out=and_31_out
  // AND_Gate and_32 has open pins: out=and_32_out
  // AND_Gate and_33 has open pins: out=and_33_out
  or or_5 (out_25, and_21_out, and_22_out, and_23_out, and_24_out, and_25_out);
  or or_6 (out_30, and_26_out, and_27_out, and_28_out, and_29_out, and_30_out, and_31_out, and_32_out, and_33_out);
  not not_13 (not_13_out, w_4);
  not not_14 (not_14_out, Y_4);
  not not_15 (not_15_out, Z_4);
  not not_16 (not_16_out, X_4);
  // AND_Gate and_34 has open pins: out=and_34_out
  // AND_Gate and_35 has open pins: out=and_35_out
  // AND_Gate and_36 has open pins: out=and_36_out
  // AND_Gate and_37 has open pins: out=and_37_out
  // AND_Gate and_38 has open pins: out=and_38_out
  // AND_Gate and_39 has open pins: out=and_39_out
  // AND_Gate and_40 has open pins: out=and_40_out
  // AND_Gate and_41 has open pins: out=and_41_out
  // AND_Gate and_42 has open pins: out=and_42_out
  // AND_Gate and_43 has open pins: out=and_43_out
  // AND_Gate and_44 has open pins: out=and_44_out
  // AND_Gate and_45 has open pins: out=and_45_out
  or or_7 (out_24, and_34_out, and_35_out, and_36_out, and_37_out, and_38_out);
  or or_8 (out_29, and_39_out, and_40_out, and_41_out, and_42_out, and_43_out, and_44_out, and_45_out);
  not not_17 (not_17_out, X);
  not not_18 (not_18_out, w);
  not not_19 (not_19_out, Y);
  not not_20 (not_20_out, Z);
  // AND_Gate and_46 has open pins: out=and_46_out
  // AND_Gate and_47 has open pins: out=and_47_out
  // AND_Gate and_48 has open pins: out=and_48_out
  // AND_Gate and_49 has open pins: out=and_49_out
  // AND_Gate and_50 has open pins: out=and_50_out
  // AND_Gate and_51 has open pins: out=and_51_out
  // AND_Gate and_52 has open pins: out=and_52_out
  // AND_Gate and_53 has open pins: out=and_53_out
  // AND_Gate and_54 has open pins: out=and_54_out
  // AND_Gate and_55 has open pins: out=and_55_out
  // AND_Gate and_56 has open pins: out=and_56_out
  or or_9 (out_23, and_46_out, and_47_out, and_48_out, and_49_out);
  or or_10 (out_28, and_50_out, and_51_out, and_52_out, and_53_out, and_54_out, and_55_out, and_56_out);

  // Notes on the sheet:
  //   LETRA A
  //   LETRA B
  //   LETRA C
  //   LETRA D
  //   LETRA E
endmodule
